// Logisim project TallerLogica-Combinatorios-individual.circ as structural Verilog: 11 circuits, main circuit verificador
module sumador_simple (
  input  A,
  input  B,
  output S,
  output Cout
);

  xor xor_1 (S, A, B);
  and and_1 (Cout, A, B);
endmodule

module sumador_completo (
  input  Cin,
  input  A,
  input  B,
  output S,
  output Cout
);

  wire sumador_simple_1_cout, sumador_simple_1_s, sumador_simple_2_cout;

  sumador_simple sumador_simple_1 (.A(A), .B(B), .S(sumador_simple_1_s), .Cout(sumador_simple_1_cout));
  sumador_simple sumador_simple_2 (.A(Cin), .B(sumador_simple_1_s), .S(S), .Cout(sumador_simple_2_cout));
  or or_1 (Cout, sumador_simple_2_cout, sumador_simple_1_cout);
endmodule

module sumador_4 (
  input  Cin,
  input  [3:0] A,
  input  [3:0] B,
  output [3:0] S,
  output Cout
);

  wire Cout0, Cout1, Cout2;

  sumador_completo sumador_completo_1 (.Cin(Cin), .A(A[0]), .B(B[0]), .S(S[0]), .Cout(Cout0));
  sumador_completo sumador_completo_2 (.Cin(Cout0), .A(A[1]), .B(B[1]), .S(S[1]), .Cout(Cout1));
  sumador_completo sumador_completo_3 (.Cin(Cout1), .A(A[2]), .B(B[2]), .S(S[2]), .Cout(Cout2));
  sumador_completo sumador_completo_4 (.Cin(Cout2), .A(A[3]), .B(B[3]), .S(S[3]), .Cout(Cout));
  Hex_Digit_Display hex_digit_display_1 (.value(S));  // open: dp

  // Notes on the sheet:
  //   LSB
  //   MSB
endmodule

module comparador_cero (
  input  [3:0] A,
  output Z
);

  wire or_1_out, or_2_out, or_3_out;

  or or_1 (or_1_out, A[0], A[1]);
  or or_2 (or_2_out, A[2], A[3]);
  or or_3 (or_3_out, or_1_out, or_2_out);
  not not_1 (Z, or_3_out);
endmodule

module sumador_flags (
  input  Cin,
  input  [3:0] A,
  input  [3:0] B,
  output [3:0] S,
  output N,
  output Z,
  output V,
  output C
);

  sumador_4 sumador_4_1 (.Cin(Cin), .A(A), .B(B), .S({N, S[2:0]}), .Cout(C));
  Hex_Digit_Display hex_digit_display_1 (.value({N, S[2:0]}));  // open: dp
  comparador_cero comparador_cero_1 (.A({N, S[2:0]}), .Z(Z));
  comp_overflow comp_overflow_1 (.c3(N), .a3(A[3]), .b3(B[3]), .O(V));

  assign S[3] = N;

  // Other names for the same wires on the sheet: MSB_A = A[3]; MSB_B = B[3]; Cout = C; MSB_S = N
endmodule

module incrementador_4 (
  input  [3:0] A,
  output [3:0] S
);

  sumador_4 sumador_4_1 (.A(A), .B(4'b0001), .S(S));  // open: Cin, Cout
  Hex_Digit_Display hex_digit_display_1 (.value(S));  // open: dp
endmodule

module inversor_4 (
  input  [3:0] A,
  input  INV,
  output [3:0] S
);

  wire [3:0] incrementador_4_1_s, not_1_out;

  not not_1 (not_1_out[0], A[0]);
  not not_2 (not_1_out[1], A[1]);
  not not_3 (not_1_out[2], A[2]);
  not not_4 (not_1_out[3], A[3]);
  Multiplexer #(.width(4)) multiplexer_1 (.in0(A), .in1(incrementador_4_1_s), .out(S), .sel(INV));
  incrementador_4 incrementador_4_1 (.A(not_1_out), .S(incrementador_4_1_s));
  Hex_Digit_Display hex_digit_display_1 (.value(S));  // open: dp
endmodule

module ALU (
  input  [3:0] A,
  input  [3:0] B,
  input  [1:0] OP,
  output N,
  output Z,
  output V,
  output C,
  output [3:0] S
);

  wire C_resta, C_suma, comparador_cero_3_z, N_and, N_or, N_resta, N_suma, not_1_out, sumador_flags_2_c,
       sumador_flags_2_v, V_resta, V_suma, Z_and, Z_or, Z_resta, Z_suma;
  wire [2:0] S_and, S_or;
  wire [3:0] not_B, S_resta, S_suma;

  assign {N_and, S_and} = A & B;  // AND_Gate and_1, 4 bits wide
  assign {N_or, S_or} = A | B;  // OR_Gate or_1, 4 bits wide
  sumador_flags sumador_flags_1 (.Cin(1'b0), .A(A), .B(B), .S(S_suma), .N(N_suma), .Z(Z_suma), .V(V_suma), .C(C_suma));
  inversor_4 inversor_4_1 (.A(B), .INV(1'b1), .S(not_B));
  sumador_flags sumador_flags_2 (
    .Cin(1'b0), .A(A), .B(not_B), .S(S_resta), .N(N_resta), .Z(Z_resta), .V(sumador_flags_2_v),
    .C(sumador_flags_2_c));
  comparador_cero comparador_cero_1 (.A({N_and, S_and}), .Z(Z_and));
  comparador_cero comparador_cero_2 (.A({N_or, S_or}), .Z(Z_or));
  not not_1 (not_1_out, sumador_flags_2_c);
  comparador_cero comparador_cero_3 (.A(B), .Z(comparador_cero_3_z));
  Multiplexer multiplexer_1 (.in0(not_1_out), .in1(1'b0), .out(C_resta), .sel(comparador_cero_3_z));
  overflow_resta overflow_resta_1 (.V_in(sumador_flags_2_v), .B(B), .V_out(V_resta));
  Multiplexer #(.select(2)) multiplexer_2 (.in0(N_suma), .in1(N_resta), .in2(N_and), .in3(N_or), .out(N), .sel(OP));
  Multiplexer #(.select(2)) multiplexer_3 (.in0(Z_suma), .in1(Z_resta), .in2(Z_and), .in3(Z_or), .out(Z), .sel(OP));
  Multiplexer #(.select(2)) multiplexer_4 (.in0(V_suma), .in1(V_resta), .in2(1'b0), .in3(1'b0), .out(V), .sel(OP));
  Multiplexer #(.select(2)) multiplexer_5 (.in0(C_suma), .in1(C_resta), .in2(1'b0), .in3(1'b0), .out(C), .sel(OP));
  Multiplexer #(.select(2), .width(4)) multiplexer_6 (
    .in0(S_suma), .in1(S_resta), .in2({N_and, S_and}), .in3({N_or, S_or}), .out(S), .sel(OP));
  Hex_Digit_Display hex_digit_display_1 (.value(S));  // open: dp

  // Other names for the same wires on the sheet: S_and[3] = N_and; S_or[3] = N_or
endmodule

module verificador (
  output [3:0] out_1,
  output [3:0] out_2,
  output [1:0] out_3,
  output halt,
  output N,
  output Z,
  output V,
  output C,
  output [3:0] res
);

  wire clock_1_out;

  Clock clock_1 (.out(clock_1_out));
  Counter #(.max('h3ff), .width(10)) counter_1 (
    .clk(clock_1_out), .carry(halt), .Q({out_3, out_2, out_1}));  // open: clr, load, up, count, D
  ALU alu_1 (.A(out_1), .B(out_2), .OP(out_3), .N(N), .Z(Z), .V(V), .C(C), .S(res));
endmodule

module overflow_resta (
  input  V_in,
  input  [3:0] B,
  output V_out
);

  wire comparador_cero_1_z, not_2_out;
  wire [3:3] not_1_out;

  not not_1 (not_1_out[3], B[3]);
  not not_2 (not_2_out, V_in);
  comparador_cero comparador_cero_1 (.A({not_1_out[3], B[2:0]}), .Z(comparador_cero_1_z));
  Multiplexer multiplexer_1 (.in0(V_in), .in1(not_2_out), .out(V_out), .sel(comparador_cero_1_z));
endmodule

module comp_overflow (
  input  c3,
  input  a3,
  input  b3,
  output O
);

  wire not_1_out, xor_1_out, xor_2_out;

  xor xor_1 (xor_1_out, c3, a3);
  not not_1 (not_1_out, xor_2_out);
  xor xor_2 (xor_2_out, a3, b3);
  and and_1 (O, xor_1_out, not_1_out);
endmodule
