// Logisim project secuenciales.circ as structural Verilog: 2 circuits, main circuit regZ
module regZ (
  input  clk,
  input  Reg_in,
  input  w,
  input  en_out,
  output Reg_Debug,
  output Reg_output
);

  wire and_1_out;

  D_Flip_Flop d_ff_1 (.D(Reg_in), .clk(and_1_out), .Q(Reg_Debug));  // open: Qn, preset, reset
  and and_1 (and_1_out, clk, w);
  assign Reg_output = en_out ? Reg_Debug : 1'bz;  // Controlled_Buffer controlled_buffer_1
endmodule

module regBank (
  input  in_1,
  input  in_2,
  input  in_3,
  input  in_4,
  input  clk,
  input  input_bit,
  input  in_7,
  input  in_8,
  input  en_input_bit,
  output R0,
  output out_11,
  output R1,
  output R2
);

  assign out_11 = en_input_bit ? input_bit : 1'bz;  // Controlled_Buffer controlled_buffer_1
  regZ regz_1 (.clk(clk), .Reg_in(out_11), .w(in_1), .en_out(in_2), .Reg_Debug(R0), .Reg_output(out_11));
  regZ regz_2 (.clk(clk), .Reg_in(out_11), .w(in_3), .en_out(in_4), .Reg_Debug(R1), .Reg_output(out_11));
  regZ regz_3 (.clk(clk), .Reg_in(out_11), .w(in_7), .en_out(in_8), .Reg_Debug(R2), .Reg_output(out_11));
endmodule
